// Logisim project cpu.circ as structural Verilog: 1 circuit, main circuit main
module main (
);

  wire ALC, ALO, ALS, and_1_out, clock_1_out, FE, HLT, IE, IRE, IRO, JMP, MAE, not_1_out, not_2_out, PCE,
       PCO, RAE, RAO, XE, XO, YE, YO, ZE, ZO;
  wire [4:0] pull_resistor_5_node;
  wire [7:0] controlled_buffer_3_out, FlagsReg_q;
  wire [8:0] InstructionStepCounter_q;
  wire [10:0] controlled_buffer_1_out, controlled_buffer_2_out, controlled_buffer_12_out,
       InstructionRegister_q, MemoryAddressRegister_q, ProgramCounter_q;
  wire [15:0] controlled_buffer_4_out, controlled_buffer_6_out, controlled_buffer_8_out,
       controlled_buffer_10_out, controlled_buffer_13_out, ram_1_dout, XReg_q, YReg_q, ZReg_q;
  wire [15:11] controlled_buffer_11_out;

  Clock clock_1 (.out(clock_1_out));
  not not_1 (not_1_out, and_1_out);
  not not_2 (not_2_out, HLT);
  Counter #(.max('h7ff), .width(11)) ProgramCounter (
    .load(JMP), .up(1'b1), .count(PCE), .clk(and_1_out), .D(controlled_buffer_1_out), .Q(ProgramCounter_q));  // open: clr, carry
  assign controlled_buffer_1_out = JMP ? controlled_buffer_2_out : 11'bz;  // Controlled_Buffer controlled_buffer_1
  Counter #(.max('hf), .width(4)) InstructionStepCounter (
    .up(1'b1), .count(1'b1), .clk(not_1_out), .Q(InstructionStepCounter_q[3:0]));  // open: clr, load, D, carry
  ROM #(.addrWidth(12), .dataWidth(20)) rom_1 (
    .addr({FlagsReg_q[2:0], InstructionStepCounter_q}),
    .data({HLT, PCE, PCO, JMP, XE, XO, YE, YO, ZE, ZO, IRE, IRO, MAE, RAE, RAO, FE, ALO, ALS, ALC, IE}));
  and and_1 (and_1_out, clock_1_out, not_2_out);
  LED led_1 (.in(pull_resistor_5_node[4]));
  LED led_2 (.in(pull_resistor_5_node[3]));
  LED led_3 (.in(pull_resistor_5_node[2]));
  assign controlled_buffer_2_out = PCO ? ProgramCounter_q : 11'bz;  // Controlled_Buffer controlled_buffer_2
  Pull_Resistor pull_resistor_1 (.node(pull_resistor_5_node[4]));
  LED led_4 (.in(pull_resistor_5_node[1]));
  LED led_5 (.in(pull_resistor_5_node[0]));
  LED led_6 (.in(controlled_buffer_2_out[10]));
  LED led_7 (.in(controlled_buffer_2_out[9]));
  Pull_Resistor pull_resistor_2 (.node(pull_resistor_5_node[3]));
  Pull_Resistor pull_resistor_3 (.node(pull_resistor_5_node[2]));
  Pull_Resistor pull_resistor_4 (.node(pull_resistor_5_node[1]));
  Pull_Resistor pull_resistor_5 (.node(pull_resistor_5_node[0]));
  LED led_8 (.in(controlled_buffer_2_out[8]));
  LED led_9 (.in(controlled_buffer_2_out[7]));
  LED led_10 (.in(controlled_buffer_2_out[6]));
  LED led_11 (.in(controlled_buffer_2_out[5]));
  Pull_Resistor pull_resistor_6 (.node(controlled_buffer_2_out[10]));
  Pull_Resistor pull_resistor_7 (.node(controlled_buffer_2_out[9]));
  Pull_Resistor pull_resistor_8 (.node(controlled_buffer_2_out[8]));
  Pull_Resistor pull_resistor_9 (.node(controlled_buffer_2_out[7]));
  Pull_Resistor pull_resistor_10 (.node(controlled_buffer_2_out[6]));
  Pull_Resistor pull_resistor_11 (.node(controlled_buffer_2_out[5]));
  LED led_12 (.in(controlled_buffer_2_out[4]));
  LED led_13 (.in(controlled_buffer_2_out[3]));
  LED led_14 (.in(controlled_buffer_2_out[2]));
  LED led_15 (.in(controlled_buffer_2_out[1]));
  Pull_Resistor pull_resistor_12 (.node(controlled_buffer_2_out[4]));
  Pull_Resistor pull_resistor_13 (.node(controlled_buffer_2_out[3]));
  Pull_Resistor pull_resistor_14 (.node(controlled_buffer_2_out[2]));
  Pull_Resistor pull_resistor_15 (.node(controlled_buffer_2_out[1]));
  Pull_Resistor pull_resistor_16 (.node(controlled_buffer_2_out[0]));
  LED led_16 (.in(controlled_buffer_2_out[0]));
  Register FlagsReg (.D(controlled_buffer_3_out), .en(FE), .clk(and_1_out), .Q(FlagsReg_q));  // open: clr
  assign controlled_buffer_3_out = FE ? {8{1'b0}} : 8'bz;  // Controlled_Buffer controlled_buffer_3
  Register #(.width(16)) XReg (.D(controlled_buffer_4_out), .en(XE), .clk(and_1_out), .Q(XReg_q));  // open: clr
  assign controlled_buffer_4_out = XE ? {pull_resistor_5_node, controlled_buffer_2_out} : 16'bz;  // Controlled_Buffer controlled_buffer_4
  assign {pull_resistor_5_node, controlled_buffer_2_out} = XO ? XReg_q : 16'bz;  // Controlled_Buffer controlled_buffer_5
  Register #(.width(16)) YReg (.D(controlled_buffer_6_out), .en(YE), .clk(and_1_out), .Q(YReg_q));  // open: clr
  assign controlled_buffer_6_out = YE ? {pull_resistor_5_node, controlled_buffer_2_out} : 16'bz;  // Controlled_Buffer controlled_buffer_6
  assign {pull_resistor_5_node, controlled_buffer_2_out} = YO ? YReg_q : 16'bz;  // Controlled_Buffer controlled_buffer_7
  Register #(.width(16)) ZReg (.D(controlled_buffer_8_out), .en(ZE), .clk(and_1_out), .Q(ZReg_q));  // open: clr
  assign controlled_buffer_8_out = ZE ? {pull_resistor_5_node, controlled_buffer_2_out} : 16'bz;  // Controlled_Buffer controlled_buffer_8
  assign {pull_resistor_5_node, controlled_buffer_2_out} = ZO ? ZReg_q : 16'bz;  // Controlled_Buffer controlled_buffer_9
  Register #(.width(16)) InstructionRegister (
    .D(controlled_buffer_10_out), .en(IRE), .clk(and_1_out),
    .Q({InstructionStepCounter_q[8:4], InstructionRegister_q}));  // open: clr
  assign controlled_buffer_10_out = IRE ? {pull_resistor_5_node, controlled_buffer_2_out} : 16'bz;  // Controlled_Buffer controlled_buffer_10
  assign {controlled_buffer_11_out, controlled_buffer_2_out} = IRO ? {InstructionStepCounter_q[8:4], InstructionRegister_q} : 16'bz;  // Controlled_Buffer controlled_buffer_11
  Register #(.width(11)) MemoryAddressRegister (
    .D(controlled_buffer_12_out), .en(MAE), .clk(and_1_out), .Q(MemoryAddressRegister_q));  // open: clr
  assign controlled_buffer_12_out = MAE ? controlled_buffer_2_out : 11'bz;  // Controlled_Buffer controlled_buffer_12
  assign controlled_buffer_13_out = RAE ? {pull_resistor_5_node, controlled_buffer_2_out} : 16'bz;  // Controlled_Buffer controlled_buffer_13
  assign {pull_resistor_5_node, controlled_buffer_2_out} = RAO ? ram_1_dout : 16'bz;  // Controlled_Buffer controlled_buffer_14
  RAM #(.addrWidth(11), .dataWidth(16), .enables("line"), .\type ("nonvolatile")) ram_1 (
    .addr(MemoryAddressRegister_q), .we(RAE), .clk(and_1_out), .din(controlled_buffer_13_out),
    .dout(ram_1_dout));
endmodule
